# Fritzing sketch flash (saved by Fritzing 0.9.1b)

parts:
  U1 = ESP8266 WiFi Module [part_number=ESP8266]
  Composant1 = FTDI Basic Programmer

nets:
  N1: U1.RXD, Composant1.RXI
  N2: U1.VCC, U1.CH_PD, Composant1.POWER
  GND: U1.GPIO_0, U1.GND, Composant1.GND
  N3: U1.TXD, Composant1.TXO

custom parts:
  ESP8266 WiFi Module: Generic WiFi Module based on the ESP8266 with onboard PCB antenna and UART communications
