# Fritzing sketch arduinoSwitch (saved by Fritzing 0.9.1b)

parts:
  Composant1 = Arduino Uno (Rev3)
  Composant2 = Arduino Leonardo (Rev3b)

nets:
  N1: Composant1.D10_PWM/SS, Composant2.D11_PWM
  N2: Composant1.D11_PWM/MOSI, Composant2.D10_PWM/A10

notes:
  La sortie de vers le PC se fait sur le port série de l'aduino UNO
